# Fritzing sketch Flight1 (saved by Fritzing 0.9.2b)

parts:
  Part1 = Arduino Mega 2560 (Rev3)  # not connected
  Part3 = Arduino GPS Shield
  Part5 = IMU Analog Combo Board - 5 Degrees of Freedom
  U2 = microSD Socket [package="Molex 502774-0891 [SMD]"]  # not connected
  U3 = MPL3115A2 [package=lga8]
  LED1 = RGB LED - (4 legs) [package="5 mm [THT]"]  # not connected
  LED2 = RGB LED - (4 legs) [package="5 mm [THT]"]  # not connected
  LED3 = RGB LED - (4 legs) [package="5 mm [THT]"]  # not connected
  LED4 = RGB LED - (4 legs) [package="5 mm [THT]"]  # not connected

nets:
  N1: Part3.N$7, Part5.XRATE
  N2: Part3.N$11, U3.INT1
  N3: Part3.N$16, U3.INT2
  N4: Part3.N$17, Part5.GND
  N5: Part3.N$25, U3.GND
  N6: Part3.N$29, Part5.YRATE
  N7: Part3.N$41, Part5.VREF
  N8: Part3.N$53, Part5.ST
  N9: Part3.N$64, U3.VDDIO
  N10: Part3.N$65, Part5.ZOUT
  N11: Part3.N$77, Part5.YOUT
