# Fritzing sketch Flight1wired (saved by Fritzing 0.9.2b)

parts:
  Part1 = Arduino Mega 2560 (Rev3)
  Part3 = Arduino GPS Shield
  U2 = microSD Socket [package="Molex 502774-0891 [SMD]"]
  LED3 = RGB LED - (4 legs) [package="5 mm [THT]"]
  T1 = TMP36 Temperature Sensor [package="TO92 [THT]"]
  R1 = Resistor [tolerance=±5% resistance=330 package=THT]
  Part6 = IMU Digital Combo Board 6DOF
  U4 = MPL3115A2 [package=lga8]
  R3 = Resistor [tolerance=±5% resistance=330 package=THT]
  R4 = Resistor [tolerance=±5% resistance=330 package=THT]
  LED4 = LED - 5mm [color="Red (633nm)" package="5 mm [THT]"]
  LED5 = LED - 5mm [color="Red (633nm)" package="5 mm [THT]"]
  LED6 = LED - 5mm [color="Red (633nm)" package="5 mm [THT]"]
  R5 = Resistor [tolerance=±5% resistance=470 package=THT]
  R7 = Resistor [tolerance=±5% resistance=470 package=THT]
  R8 = Resistor [tolerance=±5% resistance=470 package=THT]
  R9 = Resistor [tolerance=±5% resistance=470 package=THT]
  R10 = Resistor [tolerance=±5% resistance=470 package=THT]
  R11 = Resistor [tolerance=±5% resistance=470 package=THT]
  LED7 = LED - 5mm [color="Red (633nm)" package="5 mm [THT]"]
  LED8 = LED - 5mm [color="Red (633nm)" package="5 mm [THT]"]
  LED9 = LED - 5mm [color="Red (633nm)" package="5 mm [THT]"]
  R12 = Resistor [tolerance=±5% resistance=470 package=THT]  # not connected
  R13 = Resistor [tolerance=±5% resistance=470 package=THT]  # not connected
  R14 = Resistor [tolerance=±5% resistance=470 package=THT]  # not connected
  R15 = Resistor [tolerance=±5% resistance=470 package=THT]  # not connected
  R16 = Resistor [tolerance=±5% resistance=470 package=THT]  # not connected
  R17 = Resistor [tolerance=±5% resistance=470 package=THT]  # not connected
  LED10 = LED - 5mm [color="Red (633nm)" package="5 mm [THT]"]  # not connected
  LED11 = LED - 5mm [color="Red (633nm)" package="5 mm [THT]"]  # not connected
  LED12 = LED - 5mm [color="Red (633nm)" package="5 mm [THT]"]  # not connected
  LED13 = LED - 5mm [color="Red (633nm)" package="5 mm [THT]"]  # not connected
  LED14 = LED - 5mm [color="Red (633nm)" package="5 mm [THT]"]  # not connected
  LED15 = LED - 5mm [color="Red (633nm)" package="5 mm [THT]"]  # not connected

nets:
  N1: Part1.A0, T1.Vout
  N2: Part1.D15/RX3, Part6.INT1
  N3: Part1.D14/TX3, Part6.INT0
  N4: Part1.SCL, U4.SCL
  N5: Part1.SDA, Part3.N$11, U4.SDA
  GND: Part1.GND, Part3.N$64, T1.GND, Part6.GND, U4.GND, LED4.anode, LED5.anode, LED6.anode, LED7.anode, LED8.anode, LED9.anode
  N6: Part1.D13_PWM, U2.DI
  N7: Part1.D12_PWM, U2.DO
  N8: Part1.IOREF, Part3.5V, Part3.N$65, T1.+Vs, U4.VDDIO
  3V3: Part1.3V3, Part6.3.3V
  5V: Part1.5V, U2.VCC, LED3.common_anode
  N9: Part1.D0_RX0, Part3.TX
  N10: Part1.D1_TX0, Part3.RX
  N11: Part1.D22, R7.Pin_0
  N12: Part1.D24, R8.Pin_0
  N13: Part1.D26, R5.Pin_0
  N14: Part1.D30, R11.Pin_0
  N15: Part1.D32, R9.Pin_0
  N16: Part1.D34, R10.Pin_0
  N17: Part1.D51, R1.Pin_1
  N18: Part1.D52, R3.Pin_1
  N19: Part1.D53, R4.Pin_1
  N20: Part3.N$16, U4.INT1
  N21: Part3.N$17, U4.INT2
  N22: Part3.N$25, U4.CAP
  N23: LED3.red_cathode, R4.Pin_0
  N24: LED3.green_cathode, R3.Pin_0
  N25: LED3.blue_cathode, R1.Pin_0
  N26: LED4.cathode, R8.Pin_1
  N27: LED5.cathode, R5.Pin_1
  N28: LED6.cathode, R7.Pin_1
  N29: R9.Pin_1, LED8.cathode
  N30: R10.Pin_1, LED7.cathode
  N31: R11.Pin_1, LED9.cathode
